# Fritzing sketch design (saved by Fritzing 0.9.3b)

parts:
  Raspberry_Pi_1 = Raspberry Pi 3 [part_number=RPI-3-V1.2]  # not connected
  Matrix_keypad1 = KEYPAD 4x4
  Part1 = RFID-RC522-v2
  Part2 = Arduino Mega ADK (Rev3)
  part = Piezo Speaker
  Part3 = Thermal Printer
  J1 = Power Jack [package=power_jack_pth_lock]

nets:
  N1: Matrix_keypad1.col1, Part2.D22
  N2: Matrix_keypad1.col2, Part2.D23
  N3: Matrix_keypad1.col3, Part2.D24
  N4: Matrix_keypad1.col4, Part2.D25
  N5: Matrix_keypad1.row1, Part2.D26
  N6: Matrix_keypad1.row2, Part2.D27
  N7: Matrix_keypad1.row3, Part2.D28
  N8: Matrix_keypad1.row4, Part2.D29
  N9: Part1.SDA, Part2.D53/SS
  N10: Part1.SCK, Part2.D52/SCK
  N11: Part1.MOSI, Part2.D51/MOSI
  N12: Part1.MISO, Part2.D50/MISO
  GND: Part1.GND, Part2.GND, part.pin1
  N13: Part1.RST, Part2.D49
  3.3V: Part1.3.3V, Part2.5V
  N14: Part2.D19/RX1, Part3.TXD
  N15: Part2.D18/TX1, Part3.RXD
  N16: Part2.D2_PWM, part.pin2
  N17: Part3.VH, J1.PWR
  N18: Part3.GND#2, J1.GNDBREAK

notes:
  Money dispenser is comming soon...
  Arduino Mega USB Raspberry Pi

custom parts:
  KEYPAD 4x4: Matrix keypad 16 buttons, 4 rows x 4 columns
  RFID-RC522-v2: A simple China made RFID-RC522 Reader; do check the pin labels, as this is a MFRC522 based clone.
